# Fritzing sketch tonuino (saved by Fritzing 0.9.4)
perfboards: 2

parts:
  R1 = Resistor [tolerance=±5% resistance=10k package=THT]
  C1 = Ceramic Capacitor [capacitance=100nF package="100 mil [THT, multilayer]"]
  Power_plug1 = Power plug
  J7 = shrouded pin header, 12 pins [form="♂ (shrouded male)"]
  C2 = Ceramic Capacitor [capacitance=100nF package="100 mil [THT, multilayer]"]
  J1 = male pin header, 9 pins [form="♂ (male)"]
  J8 = male pin header, 9 pins [form="♂ (male)"]
  J5 = male pin header, 9 pins [form="♂ (male)"]
  J4 = male pin header, 9 pins [form="♂ (male)"]
  J9 = male pin header, 2 pins [form="♂ (male)"]
  J10 = male pin header, 2 pins [form="♂ (male)"]
  23LCV1 = 23LCV1024 [part_number=23LCV1024 package="DIP (Dual Inline) [THT]"]
  J11 = male pin header, 7 pins [form="♂ (male)"]
  SP1 = SPEAKER [package=pcb_mount_speaker]  # not connected
  RFID = male pin header, 8 pins [form="♂ (male)"]

nets:
  N1: R1.Pin_0, C1.1, J7.pin12, J4.pin8
  N2: R1.Pin_1, C2.1, J5.pin9, J10.pin1, 23LCV1.NC, RFID.pin8
  N3: C1.0, J7.pin6, C2.0, J10.pin2, 23LCV1.VSS, RFID.pin6
  N4: Power_plug1.GND, J9.pin2, J11.pin6
  N5: Power_plug1.VCC, J9.pin1, J11.pin7
  N6: J7.pin1, J4.pin2
  N7: J7.pin4, J5.pin7
  N8: J7.pin5, J5.pin8
  N9: J1.pin4, RFID.pin3
  N10: J1.pin5, RFID.pin2
  N11: J1.pin6, J11.pin2
  N12: J8.pin4, RFID.pin4
  N13: J8.pin6, J11.pin1
  N14: J5.pin4, 23LCV1.SCK
  N15: J4.pin1, RFID.pin1
  N16: J4.pin3, RFID.pin7
  N17: J4.pin4, 23LCV1.CS_
  N18: J4.pin5, 23LCV1.SO/SIO1
  N19: J4.pin6, J11.pin3
  N20: J4.pin7, 23LCV1.SI/SIO0
